// Logisim project cpu24.circ as structural Verilog: 12 circuits, main circuit main_cpu
module main_cpu (
  input  RESET,
  input  ENABLE,
  input  CLK,
  output [23:0] STEP,
  output [23:0] CURR
);

  wire alu_1_halt, and_1_out, controlled_buffer_1_out;
  wire [7:0] code_1_instr;
  wire [23:0] alu_1_new_a, alu_1_new_b, alu_1_new_c, alu_1_new_mem, alu_1_new_mem_adr, alu_1_next_step,
       mem_1_adr, mem_1_data, regi_1_a, regi_1_b, regi_1_c;

  and and_1 (and_1_out, ENABLE, ~alu_1_halt);  // AND_Gate
  assign controlled_buffer_1_out = and_1_out ? CLK : 1'bz;  // Controlled_Buffer controlled_buffer_1
  regi regi_1 (
    .new_a(alu_1_new_a), .new_b(alu_1_new_b), .new_c(alu_1_new_c), .CLK(controlled_buffer_1_out),
    .RESET(RESET), .a(regi_1_a), .b(regi_1_b), .c(regi_1_c));
  // Probe on regi_1_c
  code code_1 (
    .NEXT_STEP(alu_1_next_step), .CLK(controlled_buffer_1_out), .RESET(RESET), .INSTR(code_1_instr),
    .STEP(STEP));
  alu alu_1 (
    .INSTR(code_1_instr), .MEM_ADR(mem_1_adr), .MEM(mem_1_data), .STEP(STEP), .a(regi_1_a), .b(regi_1_b),
    .c(regi_1_c), .HALT(alu_1_halt), .NEW_MEM_ADR(alu_1_new_mem_adr), .NEW_MEM(alu_1_new_mem),
    .NEXT_STEP(alu_1_next_step), .new_a(alu_1_new_a), .new_b(alu_1_new_b), .new_c(alu_1_new_c), .CURR(CURR));
  mem mem_1 (
    .NEW_ADR(alu_1_new_mem_adr), .NEW_DATA(alu_1_new_mem), .CLK(controlled_buffer_1_out), .RESET(RESET),
    .data(mem_1_data), .ADR(mem_1_adr));

  // Notes on the sheet:
  //   CPU 24 BITS
endmodule

module alu2b (
  input  [15:0] INSTR,
  input  [23:0] A,
  input  [23:0] B,
  input  [23:0] C,
  input  [23:0] STEP,
  input  [23:0] MEM,
  input  [23:0] MEM_ADR,
  input  [23:0] K0,
  input  [23:0] K1,
  input  [23:0] K2,
  input  [23:0] K3,
  input  [23:0] K4,
  input  [23:0] K5,
  input  [23:0] K6,
  input  [23:0] K7,
  input  [23:0] K8,
  output [23:0] CALC,
  output [23:0] NEW_A,
  output [23:0] NEW_B,
  output [23:0] NEW_C,
  output [23:0] NEXT_STEP,
  output [23:0] NEW_MEM,
  output [23:0] NEW_MEM_ADR,
  output [23:0] P0,
  output [23:0] P1,
  output [23:0] P2,
  output [23:0] P3,
  output [23:0] P4,
  output [23:0] P5,
  output [23:0] P6,
  output [23:0] P7,
  output [23:0] P8,
  output [23:0] CURR
);

  wire [23:0] adder_1_out, operator_1_o;

  Adder #(.width(24)) adder_1 (.a(STEP), .b(24'h1), .out(adder_1_out));  // open: cin, cout
  operator operator_1 (.CTRL(INSTR[4:0]), .a(A), .b(B), .c(C), .o(operator_1_o));
  Multiplexer #(.select(4), .width(24), .enable("false")) multiplexer_1 (
    .in0(operator_1_o), .in1(A), .in2(B), .in3(C), .in4(adder_1_out), .in5(MEM), .in6(MEM_ADR), .in7(K0),
    .in8(K1), .in9(K2), .in10(K3), .in11(K4), .in12(K5), .in13(K6), .in14(K7), .in15(K8), .out(CURR),
    .sel(INSTR[12:9]));
  router router_1 (
    .K0({24{1'b0}}), .in_2(A), .in_3(B), .in_4(C), .in_5(adder_1_out), .in_6(MEM), .in_7(MEM_ADR), .in_8(K0),
    .in_9(K1), .in_10(K2), .in_11(K3), .in_12(K4), .in_13(K5), .in_14(K6), .in_15(K7), .in_16(K8),
    .OVERRIDE(CURR), .DEST(INSTR[8:5]), .P0(CALC), .out_20(NEW_A), .out_21(NEW_B), .out_22(NEW_C),
    .out_23(NEXT_STEP), .out_24(NEW_MEM), .out_25(NEW_MEM_ADR), .out_26(P0), .out_27(P1), .out_28(P2),
    .out_29(P3), .out_30(P4), .out_31(P5), .out_32(P6), .out_33(P7), .P15(P8));

  // Notes on the sheet:
  //   CPU
endmodule

module alu2 (
  input  [15:0] in_1,
  input  [23:0] in_2,
  input  [23:0] in_3,
  input  [23:0] in_4,
  input  [23:0] in_5,
  input  [23:0] in_6,
  input  [23:0] in_7,
  input  [23:0] in_8,
  input  [23:0] in_9,
  input  [23:0] in_10,
  input  [23:0] in_11,
  input  [23:0] in_12,
  input  [23:0] in_13,
  input  [23:0] in_14,
  input  [23:0] in_15,
  input  [23:0] in_16,
  output [23:0] out_17,
  output [23:0] out_18,
  output [23:0] out_19,
  output [23:0] out_20,
  output [23:0] out_21,
  output [23:0] out_22,
  output [23:0] out_23,
  output [23:0] out_24,
  output [23:0] out_25,
  output [23:0] out_26,
  output [23:0] out_27,
  output [23:0] out_28,
  output [23:0] out_29,
  output [23:0] out_30,
  output [23:0] out_31,
  output [23:0] out_32,
  output [23:0] out_33
);

  wire [23:0] adder_1_out, bit_extender_1_out, operator_1_o;

  Adder #(.width(24)) adder_1 (.a(in_2), .b(24'h1), .out(adder_1_out));  // open: cin, cout
  // Probe on adder_1_out
  Multiplexer #(.select(4), .width(24), .enable("false")) multiplexer_1 (
    .in0(operator_1_o), .in1(adder_1_out), .in2(in_3), .in3(in_4), .in4(in_5), .in5(in_6), .in6(in_7),
    .in7(in_8), .in8(in_9), .in9(in_10), .in10(in_11), .in11(in_12), .in12(in_13), .in13(in_14),
    .in14(in_15), .in15(in_16), .out(out_33), .sel(in_1[12:9]));
  operator operator_1 (.CTRL(in_1[4:0]), .a(in_14), .b(in_15), .c(in_16), .o(operator_1_o));
  // Probe on operator_1_o
  assign bit_extender_1_out = {{8{1'b0}}, in_1};  // Bit_Extender bit_extender_1
  // router router_1: pin names not known; wires that end beside it: in_1[8:5], out_33, bit_extender_1_out, adder_1_out, in_3, in_4, in_5, in_6, in_7, in_8, in_9, in_10, in_11, in_12, in_13, in_14, in_15, in_16, out_17, out_18, out_19, out_20, out_21, out_22, out_23, out_24, out_25, out_26, out_27, out_28, out_29, out_30, out_31, out_32
endmodule

module alu (
  input  [7:0] INSTR,
  input  [23:0] MEM_ADR,
  input  [23:0] MEM,
  input  [23:0] STEP,
  input  [23:0] a,
  input  [23:0] b,
  input  [23:0] c,
  output HALT,
  output [23:0] NEW_MEM_ADR,
  output [23:0] NEW_MEM,
  output [23:0] NEXT_STEP,
  output [23:0] new_a,
  output [23:0] new_b,
  output [23:0] new_c,
  output [23:0] CURR
);

  wire decoder_1_out1, decoder_1_out2, decoder_1_out3, decoder_1_out4, decoder_1_out5, decoder_1_out6,
       decoder_1_out7;
  wire [23:0] A_OR_MEM_o, adder_1_out, if_gate_ex_1_out_4;

  operator operator_1 (.CTRL(INSTR[4:0]), .a(a), .b(b), .c(c), .o(CURR));
  Decoder #(.select(3), .enable("false")) decoder_1 (
    .out0(HALT), .out1(decoder_1_out1), .out2(decoder_1_out2), .out3(decoder_1_out3), .out4(decoder_1_out4),
    .out5(decoder_1_out5), .out6(decoder_1_out6), .out7(decoder_1_out7), .sel(INSTR[7:5]));
  if_gate A_OR_MEM (.i(decoder_1_out4), .t(MEM), .e(a), .o(A_OR_MEM_o));
  Adder #(.width(24)) adder_1 (.a(STEP), .b(24'h1), .out(adder_1_out));  // open: cin, cout
  if_gate if_gate_1 (.i(decoder_1_out6), .t(CURR), .e(MEM_ADR), .o(NEW_MEM_ADR));
  if_gate if_gate_2 (.i(decoder_1_out1), .t(CURR), .e(A_OR_MEM_o), .o(new_a));
  if_gate if_gate_3 (.i(decoder_1_out2), .t(CURR), .e(b), .o(new_b));
  if_gate if_gate_4 (.i(decoder_1_out3), .t(CURR), .e(c), .o(new_c));
  if_gate_ex if_gate_ex_1 (.i(a), .t(adder_1_out), .e(b), .out_4(if_gate_ex_1_out_4));
  if_gate if_gate_5 (.i(decoder_1_out5), .t(CURR), .e(MEM), .o(NEW_MEM));
  if_gate if_gate_6 (.i(decoder_1_out7), .t(if_gate_ex_1_out_4), .e(adder_1_out), .o(NEXT_STEP));
endmodule

module if_gate (
  input  i,
  input  [23:0] t,
  input  [23:0] e,
  output [23:0] o
);

  wire not_1_out;

  not not_1 (not_1_out, i);
  assign o = not_1_out ? e : 24'bz;  // Controlled_Buffer controlled_buffer_1
  assign o = i ? t : 24'bz;  // Controlled_Buffer controlled_buffer_2
endmodule

module if_gate_ex (
  input  [23:0] i,
  input  [23:0] t,
  input  [23:0] e,
  output [23:0] out_4
);

  wire comparator_1_eq, not_1_out;

  Comparator #(.width(24)) comparator_1 (.a({24{1'b0}}), .b(i), .eq(comparator_1_eq));  // open: gt, lt
  not not_1 (not_1_out, comparator_1_eq);
  assign out_4 = not_1_out ? t : 24'bz;  // Controlled_Buffer controlled_buffer_1
  assign out_4 = comparator_1_eq ? e : 24'bz;  // Controlled_Buffer controlled_buffer_2
endmodule

module operator (
  input  [4:0] CTRL,
  input  [23:0] a,
  input  [23:0] b,
  input  [23:0] c,
  output [23:0] o
);

  wire comparator_1_gt, comparator_2_eq;
  wire [4:0] bit_extender_3_out, bitadder_1_out;
  wire [23:0] adder_1_out, adder_2_out, and_1_out, bit_extender_1_out, bit_extender_2_out,
       bit_extender_4_out, divider_1_rem, divider_2_out, if_gate_ex_1_out_4, if_gate_ex_2_out_4,
       if_gate_ex_3_out_4, multiplier_1_out, negator_1_out, not_1_out, or_1_out, shifter_1_out,
       subtractor_1_out, xor_1_out;

  if_gate_ex if_gate_ex_1 (.i(a), .t(b), .e(c), .out_4(if_gate_ex_1_out_4));
  if_gate_ex if_gate_ex_2 (.i(a), .t(b), .e({24{1'b0}}), .out_4(if_gate_ex_2_out_4));
  assign bit_extender_1_out = {{23{comparator_1_gt}}, comparator_1_gt};  // Bit_Extender bit_extender_1
  Comparator #(.width(24)) comparator_1 (.a(a), .b(b), .gt(comparator_1_gt));  // open: eq, lt
  Comparator #(.width(24)) comparator_2 (.a(a), .b(b), .eq(comparator_2_eq));  // open: gt, lt
  assign bit_extender_2_out = {{23{comparator_2_eq}}, comparator_2_eq};  // Bit_Extender bit_extender_2
  Bit_Extender #(.in_width(24), .out_width(5), .\type ("zero")) bit_extender_3 (.in(b), .out(bit_extender_3_out));
  Shifter #(.width(24)) shifter_1 (.in(a), .\dist (bit_extender_3_out), .out(shifter_1_out));
  assign xor_1_out = a ^ b;  // XOR_Gate xor_1, 24 bits wide
  assign or_1_out = a | b;  // OR_Gate or_1, 24 bits wide
  assign and_1_out = a & b;  // AND_Gate and_1, 24 bits wide
  Divider #(.width(24)) divider_1 (.a(a), .b(b), .rem(divider_1_rem));  // open: out, upper
  Divider #(.width(24)) divider_2 (.a(a), .b(b), .out(divider_2_out));  // open: upper, rem
  Multiplier #(.width(24)) multiplier_1 (.a(a), .b(b), .out(multiplier_1_out));  // open: cin, cout
  Subtractor #(.width(24)) subtractor_1 (.a(a), .b(b), .out(subtractor_1_out));  // open: bin, bout
  Adder #(.width(24)) adder_1 (.a(a), .b(b), .out(adder_1_out));  // open: cin, cout
  BitAdder #(.width(24)) bitadder_1 (.in0(a), .out(bitadder_1_out));
  assign bit_extender_4_out = {{19{1'b0}}, bitadder_1_out};  // Bit_Extender bit_extender_4
  Adder #(.width(24)) adder_2 (.a(a), .b(24'h1), .out(adder_2_out));  // open: cin, cout
  if_gate_ex if_gate_ex_3 (.i(a), .t({24{1'b0}}), .e({24{1'b1}}), .out_4(if_gate_ex_3_out_4));
  Negator #(.width(24)) negator_1 (.in(a), .out(negator_1_out));
  assign not_1_out = ~a;  // NOT_Gate not_1, 24 bits wide
  Multiplexer #(.select(5), .width(24), .enable("false")) multiplexer_1 (
    .in0({24{1'b0}}), .in1({24{1'b1}}), .in2(a), .in3(b), .in4(c), .in5(not_1_out), .in6(negator_1_out),
    .in7(if_gate_ex_3_out_4), .in8(adder_2_out), .in9(bit_extender_4_out), .in10(adder_1_out),
    .in11(subtractor_1_out), .in12(multiplier_1_out), .in13(divider_2_out), .in14(divider_1_rem),
    .in15(and_1_out), .in16(or_1_out), .in17(xor_1_out), .in18(shifter_1_out), .in19(bit_extender_2_out),
    .in20(bit_extender_1_out), .in21(if_gate_ex_2_out_4), .in22(if_gate_ex_1_out_4), .out(o), .sel(CTRL));  // open: in23, in24, in25, in26, in27, in28, in29, in30, in31
endmodule

module mem (
  input  [23:0] NEW_ADR,
  input  [23:0] NEW_DATA,
  input  CLK,
  input  RESET,
  output [23:0] data,
  output [23:0] ADR
);

  Register #(.width(24), .trigger("falling")) register_1 (.D(NEW_ADR), .clk(CLK), .Q(ADR), .clr(RESET));  // open: en
  RAM #(.addrWidth(24), .dataWidth(24), .trigger("falling"), .databus("bibus")) ram_1 (
    .addr(ADR), .we(1'b1), .oe(1'b1), .clk(CLK), .din(NEW_DATA), .dout(data));
endmodule

module code (
  input  [23:0] NEXT_STEP,
  input  CLK,
  input  RESET,
  output [7:0] INSTR,
  output [23:0] STEP
);

  Register #(.width(24), .trigger("falling")) register_1 (.D(NEXT_STEP), .clk(CLK), .Q(STEP), .clr(RESET));  // open: en
  ROM #(.addrWidth(24)) rom_1 (.addr(STEP), .data(INSTR));

  // Notes on the sheet:
  //   contents of rom_1 (hex, n*v repeats v):
  //   6*e7 ee 0 248*e7
endmodule

module regi (
  input  [23:0] new_a,
  input  [23:0] new_b,
  input  [23:0] new_c,
  input  CLK,
  input  RESET,
  output [23:0] a,
  output [23:0] b,
  output [23:0] c
);

  wire undriven;

  Register #(.width(24), .trigger("falling")) register_1 (.D(new_a), .clk(CLK), .Q(a), .clr(RESET));  // open: en
  Register #(.width(24), .trigger("falling")) register_2 (.D(new_b), .en(undriven), .clk(CLK), .Q(b), .clr(RESET));
  Register #(.width(24), .trigger("falling")) register_3 (.D(new_c), .clk(CLK), .Q(c), .clr(RESET));  // open: en
endmodule

module router (
  input  [23:0] K0,
  input  [23:0] in_2,
  input  [23:0] in_3,
  input  [23:0] in_4,
  input  [23:0] in_5,
  input  [23:0] in_6,
  input  [23:0] in_7,
  input  [23:0] in_8,
  input  [23:0] in_9,
  input  [23:0] in_10,
  input  [23:0] in_11,
  input  [23:0] in_12,
  input  [23:0] in_13,
  input  [23:0] in_14,
  input  [23:0] in_15,
  input  [23:0] in_16,
  input  [23:0] OVERRIDE,
  input  [3:0] DEST,
  output [23:0] P0,
  output [23:0] out_20,
  output [23:0] out_21,
  output [23:0] out_22,
  output [23:0] out_23,
  output [23:0] out_24,
  output [23:0] out_25,
  output [23:0] out_26,
  output [23:0] out_27,
  output [23:0] out_28,
  output [23:0] out_29,
  output [23:0] out_30,
  output [23:0] out_31,
  output [23:0] out_32,
  output [23:0] out_33,
  output [23:0] P15
);

  wire decoder_1_out0, decoder_1_out1, decoder_1_out2, decoder_1_out3, decoder_1_out4, decoder_1_out5,
       decoder_1_out6, decoder_1_out7, decoder_1_out8, decoder_1_out9, decoder_1_out10, decoder_1_out11,
       decoder_1_out12, decoder_1_out13, decoder_1_out14, decoder_1_out15, not_1_out, not_2_out, not_3_out,
       not_4_out, not_5_out, not_6_out, not_7_out, not_8_out, not_9_out, not_10_out, not_11_out, not_12_out,
       not_13_out, not_14_out, not_15_out, not_16_out;

  Decoder #(.select(4), .enable("false")) decoder_1 (
    .out0(decoder_1_out0), .out1(decoder_1_out1), .out2(decoder_1_out2), .out3(decoder_1_out3),
    .out4(decoder_1_out4), .out5(decoder_1_out5), .out6(decoder_1_out6), .out7(decoder_1_out7),
    .out8(decoder_1_out8), .out9(decoder_1_out9), .out10(decoder_1_out10), .out11(decoder_1_out11),
    .out12(decoder_1_out12), .out13(decoder_1_out13), .out14(decoder_1_out14), .out15(decoder_1_out15),
    .sel(DEST));
  not not_1 (not_1_out, decoder_1_out0);
  assign P0 = not_1_out ? K0 : 24'bz;  // Controlled_Buffer controlled_buffer_1
  not not_2 (not_2_out, decoder_1_out1);
  assign out_20 = not_2_out ? in_2 : 24'bz;  // Controlled_Buffer controlled_buffer_2
  not not_3 (not_3_out, decoder_1_out2);
  assign out_21 = not_3_out ? in_3 : 24'bz;  // Controlled_Buffer controlled_buffer_3
  not not_4 (not_4_out, decoder_1_out3);
  assign out_22 = not_4_out ? in_4 : 24'bz;  // Controlled_Buffer controlled_buffer_4
  not not_5 (not_5_out, decoder_1_out4);
  assign out_23 = not_5_out ? in_5 : 24'bz;  // Controlled_Buffer controlled_buffer_5
  not not_6 (not_6_out, decoder_1_out5);
  assign out_24 = not_6_out ? in_6 : 24'bz;  // Controlled_Buffer controlled_buffer_6
  not not_7 (not_7_out, decoder_1_out6);
  assign out_25 = not_7_out ? in_7 : 24'bz;  // Controlled_Buffer controlled_buffer_7
  not not_8 (not_8_out, decoder_1_out7);
  assign out_26 = not_8_out ? in_8 : 24'bz;  // Controlled_Buffer controlled_buffer_8
  not not_9 (not_9_out, decoder_1_out8);
  assign out_27 = not_9_out ? in_9 : 24'bz;  // Controlled_Buffer controlled_buffer_9
  not not_10 (not_10_out, decoder_1_out9);
  assign out_28 = not_10_out ? in_10 : 24'bz;  // Controlled_Buffer controlled_buffer_10
  not not_11 (not_11_out, decoder_1_out10);
  assign out_29 = not_11_out ? in_11 : 24'bz;  // Controlled_Buffer controlled_buffer_11
  not not_12 (not_12_out, decoder_1_out11);
  assign out_30 = not_12_out ? in_12 : 24'bz;  // Controlled_Buffer controlled_buffer_12
  not not_13 (not_13_out, decoder_1_out12);
  assign out_31 = not_13_out ? in_13 : 24'bz;  // Controlled_Buffer controlled_buffer_13
  not not_14 (not_14_out, decoder_1_out13);
  assign out_32 = not_14_out ? in_14 : 24'bz;  // Controlled_Buffer controlled_buffer_14
  not not_15 (not_15_out, decoder_1_out14);
  assign out_33 = not_15_out ? in_15 : 24'bz;  // Controlled_Buffer controlled_buffer_15
  not not_16 (not_16_out, decoder_1_out15);
  assign P15 = not_16_out ? in_16 : 24'bz;  // Controlled_Buffer controlled_buffer_16
  assign P0 = decoder_1_out0 ? OVERRIDE : 24'bz;  // Controlled_Buffer controlled_buffer_17
  assign out_20 = decoder_1_out1 ? OVERRIDE : 24'bz;  // Controlled_Buffer controlled_buffer_18
  assign out_21 = decoder_1_out2 ? OVERRIDE : 24'bz;  // Controlled_Buffer controlled_buffer_19
  assign out_22 = decoder_1_out3 ? OVERRIDE : 24'bz;  // Controlled_Buffer controlled_buffer_20
  assign out_23 = decoder_1_out4 ? OVERRIDE : 24'bz;  // Controlled_Buffer controlled_buffer_21
  assign out_24 = decoder_1_out5 ? OVERRIDE : 24'bz;  // Controlled_Buffer controlled_buffer_22
  assign out_25 = decoder_1_out6 ? OVERRIDE : 24'bz;  // Controlled_Buffer controlled_buffer_23
  assign out_26 = decoder_1_out7 ? OVERRIDE : 24'bz;  // Controlled_Buffer controlled_buffer_24
  assign out_27 = decoder_1_out8 ? OVERRIDE : 24'bz;  // Controlled_Buffer controlled_buffer_25
  assign out_28 = decoder_1_out9 ? OVERRIDE : 24'bz;  // Controlled_Buffer controlled_buffer_26
  assign out_29 = decoder_1_out10 ? OVERRIDE : 24'bz;  // Controlled_Buffer controlled_buffer_27
  assign out_30 = decoder_1_out11 ? OVERRIDE : 24'bz;  // Controlled_Buffer controlled_buffer_28
  assign out_31 = decoder_1_out12 ? OVERRIDE : 24'bz;  // Controlled_Buffer controlled_buffer_29
  assign out_32 = decoder_1_out13 ? OVERRIDE : 24'bz;  // Controlled_Buffer controlled_buffer_30
  assign out_33 = decoder_1_out14 ? OVERRIDE : 24'bz;  // Controlled_Buffer controlled_buffer_31
  assign P15 = decoder_1_out15 ? OVERRIDE : 24'bz;  // Controlled_Buffer controlled_buffer_32
endmodule

module test (
  input  in_1,
  input  in_2
);

  wire clock_1_out, undriven, undriven_2;
  wire [6:0] counter_1_q;
  wire [23:0] main_cpu_1_step;

  Counter #(.width(7), .max('h7f)) counter_1 (
    .clk(clock_1_out), .Q(counter_1_q));  // open: clr, load, up, count, D, carry
  Clock clock_1 (.out(clock_1_out));
  main_cpu main_cpu_1 (.RESET(in_1), .ENABLE(in_2), .CLK(clock_1_out), .STEP(main_cpu_1_step));  // open: CURR
  // Probe on main_cpu_1_step
  TTY tty_1 (.data(counter_1_q), .clk(clock_1_out), .we(undriven), .clr(undriven_2));
  alu2b alu2b_1 ();  // open: INSTR, A, B, C, STEP, MEM, MEM_ADR, K0, K1, K2, K3, K4, K5, K6, K7, K8, CALC, NEW_A, NEW_B, NEW_C, NEXT_STEP, NEW_MEM, NEW_MEM_ADR, P0, P1, P2, P3, P4, P5, P6, P7, P8, CURR
endmodule
